// Logisim project muxrisccore.circ as structural Verilog: 4 circuits, main circuit main
module main (
);

  wire clock_1_out;
  wire [16:0] bitselector_1_out;
  wire [63:0] chip_1_output1, ram_1_dout;

  RAM #(.addrWidth(17), .dataWidth(64), .trigger("falling"), .\type ("nonvolatile")) ram_1 (
    .addr(bitselector_1_out), .clk(clock_1_out), .dout(ram_1_dout));  // open: we, oe, din
  BitSelector #(.group(17), .width(64)) bitselector_1 (.in(chip_1_output1), .out(bitselector_1_out), .sel(2'b00));
  Clock clock_1 (.out(clock_1_out));
  chip chip_1 (
    .input1(ram_1_dout), .output1(chip_1_output1));  // open: input2, input3, input4, input5, input6, input7, input8, input9, input10, input11, input12, input13, input14, input15, input16, output2, output3, output4, output5, output6, output7, output8, output9, output10, output11, output12, output13, output14, output15, output16
endmodule

module registry (
  input  [63:0] value,
  input  update,
  input  [15:0] regX,
  input  [15:0] regY,
  input  [15:0] regZ,
  input  [63:0] coreout0,
  input  [63:0] clockin0,
  input  [63:0] freqin0,
  input  [63:0] input0,
  input  [63:0] input1r,
  input  [63:0] input2r,
  input  [63:0] input3r,
  input  [63:0] input4r,
  input  [63:0] input5r,
  input  [63:0] input6r,
  input  [63:0] input7r,
  input  [63:0] input8r,
  input  [63:0] input9r,
  input  [63:0] input10r,
  input  [63:0] input11r,
  input  [63:0] input12r,
  input  [63:0] input13r,
  input  [63:0] input14r,
  input  [63:0] input15r,
  input  [63:0] input16r,
  input  [63:0] input1d,
  input  [63:0] input2d,
  input  [63:0] input3d,
  input  [63:0] input4d,
  input  [63:0] input5d,
  input  [63:0] input6d,
  input  [63:0] input7d,
  input  [63:0] input8d,
  input  [63:0] input9d,
  input  [63:0] input10d,
  input  [63:0] input11d,
  input  [63:0] input12d,
  input  [63:0] input13d,
  input  [63:0] input14d,
  input  [63:0] input15d,
  input  [63:0] input16d,
  output [63:0] regXout,
  output [63:0] regYout,
  output [63:0] regZout,
  output [63:0] corein0,
  output [63:0] clockout0,
  output [63:0] freqout0,
  output [63:0] output0,
  output [63:0] output1r,
  output [63:0] output2r,
  output [63:0] output3r,
  output [63:0] output4r,
  output [63:0] output5r,
  output [63:0] output6r,
  output [63:0] output7r,
  output [63:0] output8r,
  output [63:0] output9r,
  output [63:0] output10r,
  output [63:0] output11r,
  output [63:0] output12r,
  output [63:0] output13r,
  output [63:0] output14r,
  output [63:0] output15r,
  output [63:0] output16r,
  output [63:0] output1d,
  output [63:0] output2d,
  output [63:0] output3d,
  output [63:0] output4d,
  output [63:0] output5d,
  output [63:0] output6d,
  output [63:0] output7d,
  output [63:0] output8d,
  output [63:0] output9d,
  output [63:0] output10d,
  output [63:0] output11d,
  output [63:0] output12d,
  output [63:0] output13d,
  output [63:0] output14d,
  output [63:0] output15d,
  output [63:0] output16d
);

  wire clock_1_out, clock_2_out, clock_4_out, clock_5_out, clock_6_out, clock_7_out, clock_8_out,
       clock_9_out, clock_10_out, clock_11_out, clock_12_out, clock_13_out, clock_14_out, clock_15_out,
       clock_16_out, clock_17_out, clock_18_out, clock_19_out, clock_20_out, clock_21_out, clock_22_out,
       clock_23_out, clock_24_out, clock_25_out, clock_26_out, clock_27_out, clock_28_out, clock_29_out,
       clock_30_out, clock_31_out, clock_32_out, clock_33_out, clock_34_out, clock_35_out, clock_36_out,
       clock_37_out, clock_38_out, clock_39_out, dualram_3_p7, u221, u222, u223, u224, u225, u226, u227,
       u228, u229, u230, u231, u232, u233, u234, u235, u236, u237, u238, u239, u240, u241, u242, u243, u244,
       u245, u246, u247, u248, u249, u250, u251, u252, u253, u254, u255, u256, updated;

  // DualRAM #(.addrWidth(16), .dataWidth(64), .enables("line")) dualram_1: pin names not known; wires that end beside it: regX, regX, regXout
  Clock clock_1 (.out(clock_1_out));
  // DualRAM #(.addrWidth(16), .dataWidth(64), .enables("line")) dualram_2: pin names not known; wires that end beside it: updated, clock_1_out, value, regY, regX, regYout
  Clock clock_2 (.out(clock_2_out));
  // DualRAM #(.addrWidth(16), .dataWidth(64), .enables("line")) dualram_3: pin names not known; wires that end beside it: updated, clock_2_out, value, regZ, regX, updated, dualram_3_p7, value, regZout
  Clock clock_3 (.out(dualram_3_p7));
  Register #(.width(64)) register_1 (.D(value), .en(u221), .clk(clock_4_out), .Q(corein0));  // open: clr
  Clock clock_4 (.out(clock_4_out));
  Register #(.width(64)) register_2 (.D(value), .en(u225), .clk(clock_5_out), .Q(output1r));  // open: clr
  Clock clock_5 (.out(clock_5_out));
  Register #(.width(64)) register_3 (.D(value), .en(u229), .clk(clock_6_out), .Q(output5r));  // open: clr
  Clock clock_6 (.out(clock_6_out));
  Register #(.width(64)) register_4 (.D(value), .en(u233), .clk(clock_7_out), .Q(output9r));  // open: clr
  Clock clock_7 (.out(clock_7_out));
  Register #(.width(64)) register_5 (.D(value), .en(u237), .clk(clock_8_out), .Q(output13r));  // open: clr
  Clock clock_8 (.out(clock_8_out));
  Register #(.width(64)) register_6 (.D(value), .en(u241), .clk(clock_9_out), .Q(output1d));  // open: clr
  Clock clock_9 (.out(clock_9_out));
  Register #(.width(64)) register_7 (.D(value), .en(u245), .clk(clock_10_out), .Q(output5d));  // open: clr
  Clock clock_10 (.out(clock_10_out));
  Register #(.width(64)) register_8 (.D(value), .en(u249), .clk(clock_11_out), .Q(output9d));  // open: clr
  Clock clock_11 (.out(clock_11_out));
  Register #(.width(64)) register_9 (.D(value), .en(u253), .clk(clock_12_out), .Q(output13d));  // open: clr
  Clock clock_12 (.out(clock_12_out));
  Register #(.width(64)) register_10 (.D(value), .en(u222), .clk(clock_13_out), .Q(clockout0));  // open: clr
  Clock clock_13 (.out(clock_13_out));
  Register #(.width(64)) register_11 (.D(value), .en(u226), .clk(clock_14_out), .Q(output2r));  // open: clr
  Clock clock_14 (.out(clock_14_out));
  Register #(.width(64)) register_12 (.D(value), .en(u230), .clk(clock_15_out), .Q(output6r));  // open: clr
  Clock clock_15 (.out(clock_15_out));
  Register #(.width(64)) register_13 (.D(value), .en(u234), .clk(clock_16_out), .Q(output10r));  // open: clr
  Clock clock_16 (.out(clock_16_out));
  Register #(.width(64)) register_14 (.D(value), .en(u238), .clk(clock_17_out), .Q(output14r));  // open: clr
  Clock clock_17 (.out(clock_17_out));
  Register #(.width(64)) register_15 (.D(value), .en(u242), .clk(clock_18_out), .Q(output2d));  // open: clr
  Clock clock_18 (.out(clock_18_out));
  Register #(.width(64)) register_16 (.D(value), .en(u246), .clk(clock_19_out), .Q(output6d));  // open: clr
  Clock clock_19 (.out(clock_19_out));
  Register #(.width(64)) register_17 (.D(value), .en(u250), .clk(clock_20_out), .Q(output10d));  // open: clr
  Clock clock_20 (.out(clock_20_out));
  Register #(.width(64)) register_18 (.D(value), .en(u254), .clk(clock_21_out), .Q(output14d));  // open: clr
  Clock clock_21 (.out(clock_21_out));
  Register #(.width(64)) register_19 (.D(value), .en(u223), .clk(clock_22_out), .Q(freqout0));  // open: clr
  Clock clock_22 (.out(clock_22_out));
  Register #(.width(64)) register_20 (.D(value), .en(u227), .clk(clock_23_out), .Q(output3r));  // open: clr
  Clock clock_23 (.out(clock_23_out));
  Register #(.width(64)) register_21 (.D(value), .en(u231), .clk(clock_24_out), .Q(output7r));  // open: clr
  Clock clock_24 (.out(clock_24_out));
  Register #(.width(64)) register_22 (.D(value), .en(u235), .clk(clock_25_out), .Q(output11r));  // open: clr
  Clock clock_25 (.out(clock_25_out));
  Register #(.width(64)) register_23 (.D(value), .en(u239), .clk(clock_26_out), .Q(output15r));  // open: clr
  Clock clock_26 (.out(clock_26_out));
  Register #(.width(64)) register_24 (.D(value), .en(u243), .clk(clock_27_out), .Q(output3d));  // open: clr
  Clock clock_27 (.out(clock_27_out));
  Register #(.width(64)) register_25 (.D(value), .en(u247), .clk(clock_28_out), .Q(output7d));  // open: clr
  Clock clock_28 (.out(clock_28_out));
  Register #(.width(64)) register_26 (.D(value), .en(u251), .clk(clock_29_out), .Q(output11d));  // open: clr
  Clock clock_29 (.out(clock_29_out));
  Register #(.width(64)) register_27 (.D(value), .en(u255), .clk(clock_30_out), .Q(output15d));  // open: clr
  Clock clock_30 (.out(clock_30_out));
  Register #(.width(64)) register_28 (.D(value), .en(u224), .clk(clock_31_out), .Q(output0));  // open: clr
  Clock clock_31 (.out(clock_31_out));
  Register #(.width(64)) register_29 (.D(value), .en(u228), .clk(clock_32_out), .Q(output4r));  // open: clr
  Clock clock_32 (.out(clock_32_out));
  Register #(.width(64)) register_30 (.D(value), .en(u232), .clk(clock_33_out), .Q(output8r));  // open: clr
  Clock clock_33 (.out(clock_33_out));
  Register #(.width(64)) register_31 (.D(value), .en(u236), .clk(clock_34_out), .Q(output12r));  // open: clr
  Clock clock_34 (.out(clock_34_out));
  Register #(.width(64)) register_32 (.D(value), .en(u240), .clk(clock_35_out), .Q(output16r));  // open: clr
  Clock clock_35 (.out(clock_35_out));
  Register #(.width(64)) register_33 (.D(value), .en(u244), .clk(clock_36_out), .Q(output4d));  // open: clr
  Clock clock_36 (.out(clock_36_out));
  Register #(.width(64)) register_34 (.D(value), .en(u248), .clk(clock_37_out), .Q(output8d));  // open: clr
  Clock clock_37 (.out(clock_37_out));
  Register #(.width(64)) register_35 (.D(value), .en(u252), .clk(clock_38_out), .Q(output12d));  // open: clr
  Clock clock_38 (.out(clock_38_out));
  Register #(.width(64)) register_36 (.D(value), .en(u256), .clk(clock_39_out), .Q(output16d));  // open: clr
  Clock clock_39 (.out(clock_39_out));

  // Other names for the same wires on the sheet: v221[63:0] = coreout0; v222[63:0] = clockin0; v223[63:0] = freqin0;
  //   v224[63:0] = input0; v225[63:0] = input1r; v226[63:0] = input2r; v227[63:0] = input3r; v228[63:0] = input4r;
  //   v229[63:0] = input5r; v230[63:0] = input6r; v231[63:0] = input7r; v232[63:0] = input8r; v233[63:0] = input9r;
  //   v234[63:0] = input10r; v235[63:0] = input11r; v236[63:0] = input12r; v237[63:0] = input13r;
  //   v238[63:0] = input14r; v239[63:0] = input15r; v240[63:0] = input16r; v241[63:0] = input1d; v242[63:0] = input2d;
  //   v243[63:0] = input3d; v244[63:0] = input4d; v245[63:0] = input5d; v246[63:0] = input6d; v247[63:0] = input7d;
  //   v248[63:0] = input8d; v249[63:0] = input9d; v250[63:0] = input10d; v251[63:0] = input11d; v252[63:0] = input12d;
  //   v253[63:0] = input13d; v254[63:0] = input14d; v255[63:0] = input15d; v256[63:0] = input16d
endmodule

module core (
  input  [63:0] corein0,
  input  [63:0] clockin0,
  input  [63:0] freqin0,
  input  [63:0] input0,
  input  [63:0] input1r,
  input  [63:0] input2r,
  input  [63:0] input3r,
  input  [63:0] input4r,
  input  [63:0] input5r,
  input  [63:0] input6r,
  input  [63:0] input7r,
  input  [63:0] input8r,
  input  [63:0] input9r,
  input  [63:0] input10r,
  input  [63:0] input11r,
  input  [63:0] input12r,
  input  [63:0] input13r,
  input  [63:0] input14r,
  input  [63:0] input1r5,
  input  [63:0] input16r,
  input  [63:0] input1d,
  input  [63:0] input2d,
  input  [63:0] input3d,
  input  [63:0] input4d,
  input  [63:0] input5d,
  input  [63:0] input6d,
  input  [63:0] input7d,
  input  [63:0] input8d,
  input  [63:0] input9d,
  input  [63:0] input10d,
  input  [63:0] input11d,
  input  [63:0] input12d,
  input  [63:0] input13d,
  input  [63:0] input14d,
  input  [63:0] input15d,
  input  [63:0] input16d,
  output [63:0] coreout0,
  output [63:0] clockout0,
  output [63:0] freqout0,
  output [63:0] output0,
  output [63:0] output1r,
  output [63:0] output2r,
  output [63:0] output3r,
  output [63:0] output4r,
  output [63:0] output5r,
  output [63:0] output6r,
  output [63:0] output7r,
  output [63:0] output8r,
  output [63:0] output9r,
  output [63:0] output10r,
  output [63:0] output11r,
  output [63:0] output12r,
  output [63:0] output13r,
  output [63:0] output14r,
  output [63:0] output15r,
  output [63:0] output16r,
  output [63:0] output1d,
  output [63:0] output2d,
  output [63:0] output3d,
  output [63:0] output4d,
  output [63:0] output5d,
  output [63:0] output6d,
  output [63:0] output7d,
  output [63:0] output8d,
  output [63:0] output9d,
  output [63:0] output10d,
  output [63:0] output11d,
  output [63:0] output12d,
  output [63:0] output13d,
  output [63:0] output14d,
  output [63:0] output15d,
  output [63:0] output16d
);

  wire adder_1_cout, and_2_out, and_3_out, and_4_out, and_5_out, and_6_out, and_10_out, bitselector_9_out,
       bitselector_13_out, bitselector_14_out, clock_1_out, clock_2_out, clock_3_out, clock_4_out,
       clock_5_out, clock_6_out, comparator_1_eq, comparator_2_eq, comparator_3_eq, comparator_4_eq,
       comparator_5_eq, comparator_6_eq, comparator_7_eq, comparator_7_lt, comparator_8_eq, comparator_9_eq,
       comparator_10_eq, comparator_11_eq, comparator_11_gt, comparator_11_lt, comparator_12_eq,
       comparator_12_lt, comparator_13_eq, counter_2_q, demultiplexer_1_out1, demultiplexer_1_out2,
       demultiplexer_1_out3, fpcomparator_1_p3, fpcomparator_1_p4, multiplexer_1_out, multiplexer_5_out,
       multiplexer_10_out, not_2_out, not_6_out, or_1_out, or_3_out, or_7_out, or_8_out, or_9_out,
       register_3_q, rgb_video_1_p1, subtractor_1_bout;
  wire [1:0] bitselector_15_out, bitselector_18_out;
  wire [3:0] bitselector_6_out, bitselector_7_out;
  wire [5:0] bitselector_8_out, bitselector_10_out, bitselector_11_out, bitselector_12_out;
  wire [7:0] bitselector_5_out, bitselector_20_out, rgb_video_1_p3, rgb_video_1_p4;
  wire [15:0] bitselector_1_out, bitselector_2_out, bitselector_3_out, bitselector_4_out;
  wire [23:0] bitselector_19_out, rgb_video_1_p5;
  wire [25:0] bitselector_16_out, bitselector_17_out, counter_3_q, multiplexer_8_out, multiplexer_9_out;
  wire [31:0] counter_1_q;
  wire [63:0] adder_1_out, and_1_out, and_7_out, and_8_out, and_9_out, bit_extender_1_out,
       bit_extender_2_out, buffer_1_out, disp1_dout, divider_1_out, divider_1_rem, fpadder_1_out,
       fpdivider_1_out, fpmultiplier_1_out, fpnegator_1_p2, fpsubtractor_1_out, fptoint_1_p1, fptoint_2_p1,
       fptoint_3_p1, fptoint_4_p1, inttofp_1_p1, multiplexer_2_out, multiplexer_3_out, multiplexer_4_out,
       multiplexer_6_out, multiplexer_7_out, multiplexer_11_out, multiplexer_12_out, multiplier_1_cout,
       multiplier_1_out, nand1_dout, nand_1_out, negator_1_out, nor_1_out, not_1_out, not_3_out, not_4_out,
       not_5_out, or_2_out, or_4_out, or_5_out, or_6_out, ram1_dout, register_1_q, register_2_q,
       registry_1_regxout, registry_1_regyout, registry_1_regzout, rom1_dout, shifter_1_out, shifter_2_out,
       shifter_3_out, shifter_4_out, shifter_5_out, shifter_6_out, shifter_7_out, shifter_8_out,
       subtractor_1_out, xnor_1_out, xor_1_out;

  BitSelector #(.group(16), .width(64)) bitselector_1 (.in(register_1_q), .out(bitselector_1_out), .sel(2'b11));
  BitSelector #(.group(16), .width(64)) bitselector_2 (.in(register_1_q), .out(bitselector_2_out), .sel(2'b10));
  BitSelector #(.group(16), .width(64)) bitselector_3 (.in(register_1_q), .out(bitselector_3_out), .sel(2'b01));
  BitSelector #(.group(16), .width(64)) bitselector_4 (.in(register_1_q), .out(bitselector_4_out), .sel(2'b00));
  Register #(.trigger("falling"), .width(64)) register_1 (
    .D(multiplexer_12_out), .en(or_1_out), .clk(clock_1_out), .Q(register_1_q));  // open: clr
  or or_1 (or_1_out, or_8_out, comparator_1_eq);
  Comparator #(.width(64)) comparator_1 (.a({64{1'b0}}), .b(register_1_q), .eq(comparator_1_eq));  // open: gt, lt
  Clock clock_1 (.out(clock_1_out));
  registry registry_1 (
    .value(multiplexer_7_out), .update(or_7_out), .regX(bitselector_1_out), .regY(bitselector_2_out),
    .regZ(bitselector_3_out), .coreout0(corein0), .clockin0(clockin0), .freqin0(freqin0), .input0(input0),
    .input1r(input1r), .input2r(input2r), .input3r(input3r), .input4r(input4r), .input5r(input5r),
    .input6r(input6r), .input7r(input7r), .input8r(input8r), .input9r(input9r), .input10r(input10r),
    .input11r(input11r), .input12r(input12r), .input13r(input13r), .input14r(input14r), .input15r(input1r5),
    .input16r(input16r), .input1d(input1d), .input2d(input2d), .input3d(input3d), .input4d(input4d),
    .input5d(input5d), .input6d(input6d), .input7d(input7d), .input8d(input8d), .input9d(input9d),
    .input10d(input10d), .input11d(input11d), .input12d(input12d), .input13d(input13d), .input14d(input14d),
    .input15d(input15d), .input16d(input16d), .regXout(registry_1_regxout), .regYout(registry_1_regyout),
    .regZout(registry_1_regzout), .corein0(coreout0), .clockout0(clockout0), .freqout0(freqout0),
    .output0(output0), .output1r(output1r), .output2r(output2r), .output3r(output3r), .output4r(output4r),
    .output5r(output5r), .output6r(output6r), .output7r(output7r), .output8r(output8r), .output9r(output9r),
    .output10r(output10r), .output11r(output11r), .output12r(output12r), .output13r(output13r),
    .output14r(output14r), .output15r(output15r), .output16r(output16r), .output1d(output1d),
    .output2d(output2d), .output3d(output3d), .output4d(output4d), .output5d(output5d), .output6d(output6d),
    .output7d(output7d), .output8d(output8d), .output9d(output9d), .output10d(output10d),
    .output11d(output11d), .output12d(output12d), .output13d(output13d), .output14d(output14d),
    .output15d(output15d), .output16d(output16d));
  BitSelector #(.group(8), .width(16)) bitselector_5 (.in(bitselector_4_out), .out(bitselector_5_out), .sel(1'b1));
  BitSelector #(.group(4), .width(16)) bitselector_6 (.in(bitselector_4_out), .out(bitselector_6_out), .sel(2'b01));
  BitSelector #(.group(4), .width(16)) bitselector_7 (.in(bitselector_4_out), .out(bitselector_7_out), .sel(2'b00));
  BitSelector #(.group(6)) bitselector_8 (.in(bitselector_5_out), .out(bitselector_8_out), .sel(1'b0));
  BitSelector #(.width(4)) bitselector_9 (.in(bitselector_6_out), .out(bitselector_9_out), .sel(2'b00));
  BitSelector #(.group(6)) bitselector_10 (.in(bitselector_5_out), .out(bitselector_10_out), .sel(1'b0));
  BitSelector #(.group(6)) bitselector_11 (.in(bitselector_5_out), .out(bitselector_11_out), .sel(1'b0));
  BitSelector #(.group(6), .width(64)) bitselector_12 (
    .in(registry_1_regzout), .out(bitselector_12_out), .sel(4'b0000));
  Comparator #(.mode("unsigned"), .width(4)) comparator_2 (
    .a(bitselector_7_out), .b(4'b0000), .eq(comparator_2_eq));  // open: gt, lt
  Counter #(.max('hffffffff), .trigger("falling"), .width(32)) counter_1 (
    .load(or_3_out), .D({32{1'b0}}), .count(comparator_2_eq), .Q(counter_1_q), .clk(clock_2_out));  // open: carry, up, clr
  Clock clock_2 (.out(clock_2_out));
  BitSelector #(.width(64)) bitselector_13 (.in(registry_1_regyout), .out(bitselector_13_out), .sel(bitselector_8_out));
  Comparator #(.mode("unsigned"), .width(4)) comparator_3 (
    .a(bitselector_7_out), .b(4'b0001), .eq(comparator_3_eq));  // open: gt, lt
  Comparator #(.mode("unsigned"), .width(4)) comparator_4 (
    .a(bitselector_7_out), .b(4'b0010), .eq(comparator_4_eq));  // open: gt, lt
  Comparator #(.mode("unsigned"), .width(4)) comparator_5 (
    .a(bitselector_7_out), .b(4'b0011), .eq(comparator_5_eq));  // open: gt, lt
  Counter #(.max('h1), .trigger("falling"), .width(1)) counter_2 (
    .load(comparator_12_eq), .D(1'b0), .count(comparator_5_eq), .Q(counter_2_q), .clk(clock_3_out));  // open: carry, up, clr
  Clock clock_3 (.out(clock_3_out));
  BitSelector #(.width(4)) bitselector_14 (.in(bitselector_6_out), .out(bitselector_14_out), .sel(2'b00));
  Comparator #(.mode("unsigned"), .width(4)) comparator_6 (
    .a(bitselector_7_out), .b(4'b0100), .eq(comparator_6_eq));  // open: gt, lt
  BitSelector #(.group(2), .width(4)) bitselector_15 (.in(bitselector_6_out), .out(bitselector_15_out), .sel(1'b0));
  Comparator #(.width(64)) comparator_7 (
    .a(registry_1_regyout), .b({64{1'b0}}), .eq(comparator_7_eq), .lt(comparator_7_lt));  // open: gt
  // FPComparator #(.fpwidth(64)) fpcomparator_1: pin names not known; wires that end beside it: registry_1_regyout, {64{1'b0}}, fpcomparator_1_p3, fpcomparator_1_p4
  Comparator #(.mode("unsigned"), .width(4)) comparator_8 (
    .a(bitselector_7_out), .b(4'b0101), .eq(comparator_8_eq));  // open: gt, lt
  assign and_1_out = registry_1_regxout & not_1_out;  // AND_Gate and_1, 64 bits wide
  Adder #(.width(64)) adder_1 (
    .a(registry_1_regzout), .b(registry_1_regyout), .out(adder_1_out), .cout(adder_1_cout));  // open: cin
  assign not_1_out = ~shifter_3_out;  // NOT_Gate not_1, 64 bits wide
  assign bit_extender_1_out = {{63{1'b0}}, adder_1_cout};  // Bit_Extender bit_extender_1
  Comparator #(.mode("unsigned"), .width(4)) comparator_9 (
    .a(bitselector_7_out), .b(4'b0110), .eq(comparator_9_eq));  // open: gt, lt
  Shifter #(.width(64)) shifter_1 (.in(registry_1_regyout), .\dist (bitselector_12_out), .out(shifter_1_out));
  Comparator #(.mode("unsigned"), .width(4)) comparator_10 (
    .a(bitselector_7_out), .b(4'b0111), .eq(comparator_10_eq));  // open: gt, lt
  FPAdder #(.fpwidth(64)) fpadder_1 (.a(registry_1_regyout), .b(registry_1_regzout), .out(fpadder_1_out));
  Comparator #(.mode("unsigned"), .width(32)) comparator_11 (
    .a(counter_1_q), .b({bitselector_2_out, bitselector_3_out}), .gt(comparator_11_gt),
    .eq(comparator_11_eq), .lt(comparator_11_lt));
  and and_2 (and_2_out, comparator_5_eq, comparator_12_lt);
  and and_3 (and_3_out, comparator_12_eq, not_2_out);
  not not_2 (not_2_out, bitselector_14_out);
  Comparator #(.mode("unsigned"), .width(1)) comparator_12 (
    .a(counter_2_q), .b(1'b1), .eq(comparator_12_eq), .lt(comparator_12_lt));  // open: gt
  and and_4 (and_4_out, comparator_12_eq, bitselector_14_out);
  assign not_3_out = ~shifter_2_out;  // NOT_Gate not_3, 64 bits wide
  Multiplexer #(.select(2)) multiplexer_1 (
    .in0(comparator_7_eq), .in1(comparator_7_lt), .in2(fpcomparator_1_p3), .in3(fpcomparator_1_p4),
    .out(multiplexer_1_out), .sel(bitselector_15_out));
  Shifter #(.width(64)) shifter_2 (.in(64'h1), .\dist (bitselector_10_out), .out(shifter_2_out));
  Multiplexer #(.select(4), .width(64)) multiplexer_2 (
    .in0(adder_1_out), .in1(or_2_out), .in2(subtractor_1_out), .in3(or_5_out), .in4(multiplier_1_out),
    .in5(multiplier_1_cout), .in6(divider_1_out), .in7(divider_1_rem), .in8(negator_1_out),
    .out(multiplexer_2_out), .sel(bitselector_6_out));  // open: in9, in10, in11, in12, in13, in14, in15
  assign or_2_out = and_1_out | shifter_3_out;  // OR_Gate or_2, 64 bits wide
  Shifter #(.width(64)) shifter_3 (.in(bit_extender_1_out), .\dist (bitselector_11_out), .out(shifter_3_out));
  Multiplexer #(.select(4), .width(64)) multiplexer_3 (
    .in0(shifter_1_out), .in1(shifter_4_out), .in2(shifter_5_out), .in3(shifter_7_out), .in4(shifter_8_out),
    .in5(buffer_1_out), .in6(not_5_out), .in7(or_6_out), .in8(and_9_out), .in9(nand_1_out), .in10(nor_1_out),
    .in11(xor_1_out), .in12(xnor_1_out), .out(multiplexer_3_out), .sel(bitselector_6_out));  // open: in13, in14, in15
  Shifter #(.shift("lr"), .width(64)) shifter_4 (
    .in(registry_1_regyout), .\dist (bitselector_12_out), .out(shifter_4_out));
  Multiplexer #(.select(4), .width(64)) multiplexer_4 (
    .in0(fpadder_1_out), .in1(fpsubtractor_1_out), .in2(fpmultiplier_1_out), .in3(fpdivider_1_out),
    .in4(fpnegator_1_p2), .in5(inttofp_1_p1), .in6(fptoint_1_p1), .in7(fptoint_2_p1), .in8(fptoint_3_p1),
    .in9(fptoint_4_p1), .out(multiplexer_4_out), .sel(bitselector_6_out));  // open: in10, in11, in12, in13, in14, in15
  FPSubtractor #(.fpwidth(64)) fpsubtractor_1 (
    .a(registry_1_regyout), .b(registry_1_regzout), .out(fpsubtractor_1_out));
  or or_3 (or_3_out, comparator_11_gt, comparator_11_eq);
  and and_5 (and_5_out, comparator_11_lt, comparator_2_eq);
  and and_6 (and_6_out, bitselector_13_out, comparator_3_eq);
  assign and_7_out = registry_1_regxout & not_3_out;  // AND_Gate and_7, 64 bits wide
  assign or_4_out = and_7_out | shifter_2_out;  // OR_Gate or_4, 64 bits wide
  Subtractor #(.width(64)) subtractor_1 (
    .a(registry_1_regyout), .b(registry_1_regzout), .out(subtractor_1_out), .bout(subtractor_1_bout));  // open: bin
  Shifter #(.shift("ar"), .width(64)) shifter_5 (
    .in(registry_1_regyout), .\dist (bitselector_12_out), .out(shifter_5_out));
  FPMultiplier #(.fpwidth(64)) fpmultiplier_1 (
    .a(registry_1_regyout), .b(registry_1_regzout), .out(fpmultiplier_1_out));
  Multiplexer multiplexer_5 (.in0(and_6_out), .in1(comparator_3_eq), .out(multiplexer_5_out), .sel(bitselector_9_out));
  Multiplexer #(.width(64)) multiplexer_6 (
    .in0(and_7_out), .in1(or_4_out), .out(multiplexer_6_out), .sel(multiplexer_1_out));
  assign and_8_out = registry_1_regxout & not_4_out;  // AND_Gate and_8, 64 bits wide
  assign not_4_out = ~shifter_6_out;  // NOT_Gate not_4, 64 bits wide
  assign bit_extender_2_out = {{63{1'b0}}, subtractor_1_bout};  // Bit_Extender bit_extender_2
  Shifter #(.width(64)) shifter_6 (.in(bit_extender_2_out), .\dist (bitselector_11_out), .out(shifter_6_out));
  Shifter #(.shift("rl"), .width(64)) shifter_7 (
    .in(registry_1_regyout), .\dist (bitselector_12_out), .out(shifter_7_out));
  FPDivider #(.fpwidth(64)) fpdivider_1 (.a(registry_1_regyout), .b(registry_1_regzout), .out(fpdivider_1_out));
  assign or_5_out = and_8_out | shifter_6_out;  // OR_Gate or_5, 64 bits wide
  assign not_5_out = ~registry_1_regyout;  // NOT_Gate not_5, 64 bits wide
  assign or_6_out = registry_1_regyout | registry_1_regzout;  // OR_Gate or_6, 64 bits wide
  assign buffer_1_out = registry_1_regyout;  // Buffer buffer_1, 64 bits wide
  Shifter #(.shift("rr"), .width(64)) shifter_8 (
    .in(registry_1_regyout), .\dist (bitselector_12_out), .out(shifter_8_out));
  // FPNegator #(.fpwidth(64)) fpnegator_1: pin names not known; wires that end beside it: registry_1_regyout, fpnegator_1_p2, registry_1_regyout
  // IntToFP #(.fpwidth(64), .width(64)) inttofp_1: pin names not known; wires that end beside it: inttofp_1_p1, registry_1_regyout
  Multiplier #(.width(64)) multiplier_1 (
    .a(registry_1_regyout), .b(registry_1_regzout), .out(multiplier_1_out), .cout(multiplier_1_cout));  // open: cin
  assign nand_1_out = ~(registry_1_regyout & registry_1_regzout);  // NAND_Gate nand_1, 64 bits wide
  assign nor_1_out = ~(registry_1_regyout | registry_1_regzout);  // NOR_Gate nor_1, 64 bits wide
  assign and_9_out = registry_1_regyout & registry_1_regzout;  // AND_Gate and_9, 64 bits wide
  // FPToInt #(.fpwidth(64), .width(64)) fptoint_1: pin names not known; wires that end beside it: fptoint_1_p1, registry_1_regyout
  Divider #(.mode("twosComplement"), .width(64)) divider_1 (
    .a(registry_1_regyout), .b(registry_1_regzout), .out(divider_1_out), .rem(divider_1_rem));  // open: upper
  assign xnor_1_out = ~(registry_1_regyout ^ registry_1_regzout);  // XNOR_Gate xnor_1, 64 bits wide
  assign xor_1_out = registry_1_regyout ^ registry_1_regzout;  // XOR_Gate xor_1, 64 bits wide
  // FPToInt #(.fpwidth(64), .mode("floor"), .width(64)) fptoint_2: pin names not known; wires that end beside it: fptoint_2_p1, registry_1_regyout
  Negator #(.width(64)) negator_1 (.in(registry_1_regyout), .out(negator_1_out));
  // FPToInt #(.fpwidth(64), .mode("ceil"), .width(64)) fptoint_3: pin names not known; wires that end beside it: fptoint_3_p1, registry_1_regyout
  // FPToInt #(.fpwidth(64), .mode("truncate"), .width(64)) fptoint_4: pin names not known; wires that end beside it: fptoint_4_p1
  or or_7 (or_7_out, comparator_4_eq, and_3_out, comparator_6_eq, comparator_8_eq, comparator_9_eq, comparator_10_eq);
  or or_8 (or_8_out, comparator_2_eq, comparator_3_eq, comparator_4_eq, comparator_12_eq, comparator_6_eq, comparator_8_eq, comparator_9_eq, comparator_10_eq);
  Multiplexer #(.select(4), .width(64)) multiplexer_7 (
    .in0(multiplexer_12_out), .in1(multiplexer_12_out),
    .in2({{32{1'b0}}, bitselector_2_out, bitselector_3_out}), .in3(multiplexer_12_out),
    .in4(multiplexer_6_out), .in5(multiplexer_2_out), .in6(multiplexer_3_out), .in7(multiplexer_4_out),
    .out(multiplexer_7_out), .sel(bitselector_7_out));  // open: in8, in9, in10, in11, in12, in13, in14, in15
  BitSelector #(.group(26), .width(64)) bitselector_16 (.in(registry_1_regxout), .out(bitselector_16_out), .sel(2'b00));
  or or_9 (or_9_out, and_5_out, comparator_12_eq);
  Register #(.width(64)) register_2 (
    .D(registry_1_regyout), .en(and_2_out), .clk(clock_4_out), .Q(register_2_q));  // open: clr
  Clock clock_4 (.out(clock_4_out));
  Counter #(.max('h3ffffff), .width(26)) counter_3 (
    .load(multiplexer_5_out), .D(bitselector_16_out), .count(not_6_out), .Q(counter_3_q), .clk(clock_5_out));  // open: carry, up, clr
  not not_6 (not_6_out, or_9_out);
  Clock clock_5 (.out(clock_5_out));
  BitSelector #(.group(26), .width(64)) bitselector_17 (.in(register_2_q), .out(bitselector_17_out), .sel(2'b00));
  Register #(.width(1)) register_3 (.D(and_2_out), .en(1'b1), .clk(clock_4_out), .Q(register_3_q));  // open: clr
  Multiplexer #(.width(26)) multiplexer_8 (
    .in0(counter_3_q), .in1(bitselector_17_out), .out(multiplexer_8_out), .sel(register_3_q));
  Multiplexer #(.select(4), .width(26)) multiplexer_9 (
    .in0(counter_3_q), .in1(counter_3_q), .in2(counter_3_q), .in3(multiplexer_8_out), .in4(counter_3_q),
    .in5(counter_3_q), .in6(counter_3_q), .in7(counter_3_q), .out(multiplexer_9_out), .sel(bitselector_7_out));  // open: in8, in9, in10, in11, in12, in13, in14, in15
  Multiplexer #(.select(4)) multiplexer_10 (
    .in0(1'b0), .in1(1'b0), .in2(1'b0), .in3(and_4_out), .in4(1'b0), .in5(1'b0), .in6(1'b0), .in7(1'b0),
    .out(multiplexer_10_out), .sel(bitselector_7_out));  // open: in8, in9, in10, in11, in12, in13, in14, in15
  Multiplexer #(.select(4), .width(64)) multiplexer_11 (
    .in0({64{1'b0}}), .in1({64{1'b0}}), .in2({64{1'b0}}), .in3(registry_1_regxout), .in4({64{1'b0}}),
    .in5({64{1'b0}}), .in6({64{1'b0}}), .in7({64{1'b0}}), .out(multiplexer_11_out), .sel(bitselector_7_out));  // open: in8, in9, in10, in11, in12, in13, in14, in15
  BitSelector #(.group(2), .width(26)) bitselector_18 (.in(multiplexer_9_out), .out(bitselector_18_out), .sel(4'b1100));
  BitSelector #(.group(24), .width(26)) bitselector_19 (.in(multiplexer_9_out), .out(bitselector_19_out), .sel(1'b0));
  Clock clock_6 (.out(clock_6_out));
  Demultiplexer #(.select(2)) demultiplexer_1 (
    .out1(demultiplexer_1_out1), .out2(demultiplexer_1_out2), .out3(demultiplexer_1_out3),
    .in(multiplexer_10_out), .sel(bitselector_18_out));  // open: out0
  RAM #(.addrWidth(24), .dataWidth(64), .enables("line"), .\type ("nonvolatile")) rom1 (
    .addr(bitselector_19_out), .clk(clock_6_out), .dout(rom1_dout));  // open: we, din
  RAM #(.addrWidth(24), .dataWidth(64), .enables("line"), .\type ("nonvolatile")) ram1 (
    .addr(bitselector_19_out), .we(demultiplexer_1_out1), .clk(clock_6_out), .din(multiplexer_11_out),
    .dout(ram1_dout));
  RAM #(.addrWidth(24), .dataWidth(64), .enables("line"), .\type ("nonvolatile")) disp1 (
    .addr(bitselector_19_out), .we(demultiplexer_1_out2), .clk(clock_6_out), .din(multiplexer_11_out),
    .dout(disp1_dout));
  RAM #(.addrWidth(24), .dataWidth(64), .enables("line"), .\type ("nonvolatile")) nand1 (
    .addr(bitselector_19_out), .we(demultiplexer_1_out3), .clk(clock_6_out), .din(multiplexer_11_out),
    .dout(nand1_dout));
  Multiplexer #(.select(2), .width(64)) multiplexer_12 (
    .in0(rom1_dout), .in1(ram1_dout), .in2(disp1_dout), .in3(nand1_dout), .out(multiplexer_12_out),
    .sel(bitselector_18_out));
  BitSelector #(.group(8), .width(24)) bitselector_20 (.in(bitselector_19_out), .out(bitselector_20_out), .sel(2'b10));
  Comparator #(.mode("unsigned")) comparator_13 (
    .a(bitselector_20_out), .b({8{1'b0}}), .eq(comparator_13_eq));  // open: gt, lt
  and and_10 (and_10_out, demultiplexer_1_out2, comparator_13_eq);
  // RGB_Video #(.height(256), .scale(1), .width(256)) rgb_video_1: pin names not known; wires that end beside it: rgb_video_1_p1, and_10_out, rgb_video_1_p3, rgb_video_1_p4, rgb_video_1_p5
  Clock clock_7 (.out(rgb_video_1_p1));
  BitSelector #(.group(8), .width(24)) bitselector_21 (.in(bitselector_19_out), .out(rgb_video_1_p3), .sel(2'b00));
  BitSelector #(.group(8), .width(24)) bitselector_22 (.in(bitselector_19_out), .out(rgb_video_1_p4), .sel(2'b01));
  BitSelector #(.group(8), .width(64)) bitselector_23 (
    .in(multiplexer_11_out), .out(rgb_video_1_p5[7:0]), .sel(3'b000));
  BitSelector #(.group(8), .width(64)) bitselector_24 (
    .in(multiplexer_11_out), .out(rgb_video_1_p5[15:8]), .sel(3'b010));
  BitSelector #(.group(8), .width(64)) bitselector_25 (
    .in(multiplexer_11_out), .out(rgb_video_1_p5[23:16]), .sel(3'b100));
endmodule

module chip (
  input  [63:0] input1,
  input  [63:0] input2,
  input  [63:0] input3,
  input  [63:0] input4,
  input  [63:0] input5,
  input  [63:0] input6,
  input  [63:0] input7,
  input  [63:0] input8,
  input  [63:0] input9,
  input  [63:0] input10,
  input  [63:0] input11,
  input  [63:0] input12,
  input  [63:0] input13,
  input  [63:0] input14,
  input  [63:0] input15,
  input  [63:0] input16,
  output [63:0] output1,
  output [63:0] output2,
  output [63:0] output3,
  output [63:0] output4,
  output [63:0] output5,
  output [63:0] output6,
  output [63:0] output7,
  output [63:0] output8,
  output [63:0] output9,
  output [63:0] output10,
  output [63:0] output11,
  output [63:0] output12,
  output [63:0] output13,
  output [63:0] output14,
  output [63:0] output15,
  output [63:0] output16
);

  wire clock_1_out;
  wire [63:0] c0, d1A, d1B, d1C, d1D, d1E, d1F, d1G, d2A, d2B, d2C, d2D, d2E, d2F, d2G, d3A, d3B, d3C, d3D,
       d3E, d3F, d3G, d4A, d4B, d4C, d4D, d4E, d4F, d4G, d5A, d5B, d5C, d5D, d5E, d5F, d5G, d6A, d6B, d6C,
       d6D, d6E, d6F, d6G, d7A, d7B, d7C, d7D, d7E, d7F, d7G, d8A, d8B, d8C, d8D, d8E, d8F, d8G, d9A, d9B,
       d9C, d9D, d9E, d9F, d9G, d11, d12, d13, d14, d15, d16, d17, d18, d19, d21, d22, d23, d24, d25, d26,
       d27, d28, d29, d31, d32, d33, d34, d35, d36, d37, d38, d39, d41, d42, d43, d44, d45, d46, d47, d48,
       d49, d51, d52, d53, d54, d55, d56, d57, d58, d59, d61, d62, d63, d64, d65, d66, d67, d68, d69, d71,
       d72, d73, d74, d75, d76, d77, d78, d79, d81, d82, d83, d84, d85, d86, d87, d88, d89, d91, d92, d93,
       d94, d95, d96, d97, d98, d99, dA1, dA2, dA3, dA4, dA5, dA6, dA7, dA8, dA9, dAA, dAB, dAC, dAD, dAE,
       dAF, dAG, dB1, dB2, dB3, dB4, dB5, dB6, dB7, dB8, dB9, dBA, dBB, dBC, dBD, dBE, dBF, dBG, dC1, dC2,
       dC3, dC4, dC5, dC6, dC7, dC8, dC9, dCA, dCB, dCC, dCD, dCE, dCF, dCG, dD1, dD2, dD3, dD4, dD5, dD6,
       dD7, dD8, dD9, dDA, dDB, dDC, dDD, dDE, dDF, dDG, dE1, dE2, dE3, dE4, dE5, dE6, dE7, dE8, dE9, dEA,
       dEB, dEC, dED, dEE, dEF, dEG, dF1, dF2, dF3, dF4, dF5, dF6, dF7, dF8, dF9, dFA, dFB, dFC, dFD, dFE,
       dFF, dFG, dG1, dG2, dG3, dG4, dG5, dG6, dG7, dG8, dG9, dGA, dGB, dGC, dGD, dGE, dGF, dGG, r1, r2, r3,
       r4, r5, r6, r7, r8, r9, r10, r11, r12, r13, r14, r15, r16;

  core core1 (
    .corein0(64'hf000e0000f0000), .clockin0(c0), .freqin0(64'h5000000000), .input0(input1), .input1r(r1),
    .input2r(r2), .input3r(r3), .input4r(r4), .input5r(r5), .input6r(r6), .input7r(r7), .input8r(r8),
    .input9r(r9), .input10r(r10), .input11r(r11), .input12r(r12), .input13r(r13), .input14r(r14),
    .input1r5(r15), .input16r(r16), .input1d(d11), .input2d(d12), .input3d(d13), .input4d(d14),
    .input5d(d15), .input6d(d16), .input7d(d17), .input8d(d18), .input9d(d19), .input10d(d1A),
    .input11d(d1B), .input12d(d1C), .input13d(d1D), .input14d(d1E), .input15d(d1F), .input16d(d1G),
    .output0(output1), .output1r(r1), .output1d(d11), .output2d(d21), .output3d(d31), .output4d(d41),
    .output5d(d51), .output6d(d61), .output7d(d71), .output8d(d81), .output9d(d91), .output10d(dA1),
    .output11d(dB1), .output12d(dC1), .output13d(dD1), .output14d(dE1), .output15d(dF1), .output16d(dG1));  // open: coreout0, clockout0, freqout0, output2r, output3r, output4r, output5r, output6r, output7r, output8r, output9r, output10r, output11r, output12r, output13r, output14r, output15r, output16r
  core core5 (
    .corein0(64'hf400e4000f0004), .clockin0(c0), .freqin0(64'h5000000000), .input0(input5), .input1r(r1),
    .input2r(r2), .input3r(r3), .input4r(r4), .input5r(r5), .input6r(r6), .input7r(r7), .input8r(r8),
    .input9r(r9), .input10r(r10), .input11r(r11), .input12r(r12), .input13r(r13), .input14r(r14),
    .input1r5(r15), .input16r(r16), .input1d(d51), .input2d(d52), .input3d(d53), .input4d(d54),
    .input5d(d55), .input6d(d56), .input7d(d57), .input8d(d58), .input9d(d59), .input10d(d5A),
    .input11d(d5B), .input12d(d5C), .input13d(d5D), .input14d(d5E), .input15d(d5F), .input16d(d5G),
    .output0(output5), .output5r(r5), .output1d(d15), .output2d(d25), .output3d(d35), .output4d(d45),
    .output5d(d55), .output6d(d65), .output7d(d75), .output8d(d85), .output9d(d95), .output10d(dA5),
    .output11d(dB5), .output12d(dC5), .output13d(dD5), .output14d(dE5), .output15d(dF5), .output16d(dG5));  // open: coreout0, clockout0, freqout0, output1r, output2r, output3r, output4r, output6r, output7r, output8r, output9r, output10r, output11r, output12r, output13r, output14r, output15r, output16r
  core core9 (
    .corein0(64'hf800e8000f0008), .clockin0(c0), .freqin0(64'h5000000000), .input0(input9), .input1r(r1),
    .input2r(r2), .input3r(r3), .input4r(r4), .input5r(r5), .input6r(r6), .input7r(r7), .input8r(r8),
    .input9r(r9), .input10r(r10), .input11r(r11), .input12r(r12), .input13r(r13), .input14r(r14),
    .input1r5(r15), .input16r(r16), .input1d(d91), .input2d(d92), .input3d(d93), .input4d(d94),
    .input5d(d95), .input6d(d96), .input7d(d97), .input8d(d98), .input9d(d99), .input10d(d9A),
    .input11d(d9B), .input12d(d9C), .input13d(d9D), .input14d(d9E), .input15d(d9F), .input16d(d9G),
    .output0(output9), .output9r(r9), .output1d(d19), .output2d(d29), .output3d(d39), .output4d(d49),
    .output5d(d59), .output6d(d69), .output7d(d79), .output8d(d89), .output9d(d99), .output10d(dA9),
    .output11d(dB9), .output12d(dC9), .output13d(dD9), .output14d(dE9), .output15d(dF9), .output16d(dG9));  // open: coreout0, clockout0, freqout0, output1r, output2r, output3r, output4r, output5r, output6r, output7r, output8r, output10r, output11r, output12r, output13r, output14r, output15r, output16r
  core coreD (
    .corein0(64'hfc00ec000f000c), .clockin0(c0), .freqin0(64'h5000000000), .input0(input13), .input1r(r1),
    .input2r(r2), .input3r(r3), .input4r(r4), .input5r(r5), .input6r(r6), .input7r(r7), .input8r(r8),
    .input9r(r9), .input10r(r10), .input11r(r11), .input12r(r12), .input13r(r13), .input14r(r14),
    .input1r5(r15), .input16r(r16), .input1d(dD1), .input2d(dD2), .input3d(dD3), .input4d(dD4),
    .input5d(dD5), .input6d(dD6), .input7d(dD7), .input8d(dD8), .input9d(dD9), .input10d(dDA),
    .input11d(dDB), .input12d(dDC), .input13d(dDD), .input14d(dDE), .input15d(dDF), .input16d(dDG),
    .output0(output13), .output13r(r13), .output1d(d1D), .output2d(d2D), .output3d(d3D), .output4d(d4D),
    .output5d(d5D), .output6d(d6D), .output7d(d7D), .output8d(d8D), .output9d(d9D), .output10d(dAD),
    .output11d(dBD), .output12d(dCD), .output13d(dDD), .output14d(dED), .output15d(dFD), .output16d(dGD));  // open: coreout0, clockout0, freqout0, output1r, output2r, output3r, output4r, output5r, output6r, output7r, output8r, output9r, output10r, output11r, output12r, output14r, output15r, output16r
  core core2 (
    .corein0(64'hf100e1000f0001), .clockin0(c0), .freqin0(64'h5000000000), .input0(input2), .input1r(r1),
    .input2r(r2), .input3r(r3), .input4r(r4), .input5r(r5), .input6r(r6), .input7r(r7), .input8r(r8),
    .input9r(r9), .input10r(r10), .input11r(r11), .input12r(r12), .input13r(r13), .input14r(r14),
    .input1r5(r15), .input16r(r16), .input1d(d21), .input2d(d22), .input3d(d23), .input4d(d24),
    .input5d(d25), .input6d(d26), .input7d(d27), .input8d(d28), .input9d(d29), .input10d(d2A),
    .input11d(d2B), .input12d(d2C), .input13d(d2D), .input14d(d2E), .input15d(d2F), .input16d(d2G),
    .output0(output2), .output2r(r2), .output1d(d12), .output2d(d22), .output3d(d32), .output4d(d42),
    .output5d(d52), .output6d(d62), .output7d(d72), .output8d(d82), .output9d(d92), .output10d(dA2),
    .output11d(dB2), .output12d(dC2), .output13d(dD2), .output14d(dE2), .output15d(dF2), .output16d(dG2));  // open: coreout0, clockout0, freqout0, output1r, output3r, output4r, output5r, output6r, output7r, output8r, output9r, output10r, output11r, output12r, output13r, output14r, output15r, output16r
  core core6 (
    .corein0(64'hf500e5000f0005), .clockin0(c0), .freqin0(64'h5000000000), .input0(input6), .input1r(r1),
    .input2r(r2), .input3r(r3), .input4r(r4), .input5r(r5), .input6r(r6), .input7r(r7), .input8r(r8),
    .input9r(r9), .input10r(r10), .input11r(r11), .input12r(r12), .input13r(r13), .input14r(r14),
    .input1r5(r15), .input16r(r16), .input1d(d61), .input2d(d62), .input3d(d63), .input4d(d64),
    .input5d(d65), .input6d(d66), .input7d(d67), .input8d(d68), .input9d(d69), .input10d(d6A),
    .input11d(d6B), .input12d(d6C), .input13d(d6D), .input14d(d6E), .input15d(d6F), .input16d(d6G),
    .output0(output6), .output6r(r6), .output1d(d16), .output2d(d26), .output3d(d36), .output4d(d46),
    .output5d(d56), .output6d(d66), .output7d(d76), .output8d(d86), .output9d(d96), .output10d(dA6),
    .output11d(dB6), .output12d(dC6), .output13d(dD6), .output14d(dE6), .output15d(dF6), .output16d(dG6));  // open: coreout0, clockout0, freqout0, output1r, output2r, output3r, output4r, output5r, output7r, output8r, output9r, output10r, output11r, output12r, output13r, output14r, output15r, output16r
  core coreA (
    .corein0(64'hf900e9000f0009), .clockin0(c0), .freqin0(64'h5000000000), .input0(input10), .input1r(r1),
    .input2r(r2), .input3r(r3), .input4r(r4), .input5r(r5), .input6r(r6), .input7r(r7), .input8r(r8),
    .input9r(r9), .input10r(r10), .input11r(r11), .input12r(r12), .input13r(r13), .input14r(r14),
    .input1r5(r15), .input16r(r16), .input1d(dA1), .input2d(dA2), .input3d(dA3), .input4d(dA4),
    .input5d(dA5), .input6d(dA6), .input7d(dA7), .input8d(dA8), .input9d(dA9), .input10d(dAA),
    .input11d(dAB), .input12d(dAC), .input13d(dAD), .input14d(dAE), .input15d(dAF), .input16d(dAG),
    .output0(output10), .output10r(r10), .output1d(d1A), .output2d(d2A), .output3d(d3A), .output4d(d4A),
    .output5d(d5A), .output6d(d6A), .output7d(d7A), .output8d(d8A), .output9d(d9A), .output10d(dAA),
    .output11d(dBA), .output12d(dCA), .output13d(dDA), .output14d(dEA), .output15d(dFA), .output16d(dGA));  // open: coreout0, clockout0, freqout0, output1r, output2r, output3r, output4r, output5r, output6r, output7r, output8r, output9r, output11r, output12r, output13r, output14r, output15r, output16r
  core coreE (
    .corein0(64'hfd00ed000f000d), .clockin0(c0), .freqin0(64'h5000000000), .input0(input14), .input1r(r1),
    .input2r(r2), .input3r(r3), .input4r(r4), .input5r(r5), .input6r(r6), .input7r(r7), .input8r(r8),
    .input9r(r9), .input10r(r10), .input11r(r11), .input12r(r12), .input13r(r13), .input14r(r14),
    .input1r5(r15), .input16r(r16), .input1d(dE1), .input2d(dE2), .input3d(dE3), .input4d(dE4),
    .input5d(dE5), .input6d(dE6), .input7d(dE7), .input8d(dE8), .input9d(dE9), .input10d(dEA),
    .input11d(dEB), .input12d(dEC), .input13d(dED), .input14d(dEE), .input15d(dEF), .input16d(dEG),
    .output0(output14), .output14r(r14), .output1d(d1E), .output2d(d2E), .output3d(d3E), .output4d(d4E),
    .output5d(d5E), .output6d(d6E), .output7d(d7E), .output8d(d8E), .output9d(d9E), .output10d(dAE),
    .output11d(dBE), .output12d(dCE), .output13d(dDE), .output14d(dEE), .output15d(dFE), .output16d(dGE));  // open: coreout0, clockout0, freqout0, output1r, output2r, output3r, output4r, output5r, output6r, output7r, output8r, output9r, output10r, output11r, output12r, output13r, output15r, output16r
  core core3 (
    .corein0(64'hf200e2000f0002), .clockin0(c0), .freqin0(64'h5000000000), .input0(input3), .input1r(r1),
    .input2r(r2), .input3r(r3), .input4r(r4), .input5r(r5), .input6r(r6), .input7r(r7), .input8r(r8),
    .input9r(r9), .input10r(r10), .input11r(r11), .input12r(r12), .input13r(r13), .input14r(r14),
    .input1r5(r15), .input16r(r16), .input1d(d31), .input2d(d32), .input3d(d33), .input4d(d34),
    .input5d(d35), .input6d(d36), .input7d(d37), .input8d(d38), .input9d(d39), .input10d(d3A),
    .input11d(d3B), .input12d(d3C), .input13d(d3D), .input14d(d3E), .input15d(d3F), .input16d(d3G),
    .output0(output3), .output3r(r3), .output1d(d13), .output2d(d23), .output3d(d33), .output4d(d43),
    .output5d(d53), .output6d(d63), .output7d(d73), .output8d(d83), .output9d(d93), .output10d(dA3),
    .output11d(dB3), .output12d(dC3), .output13d(dD3), .output14d(dE3), .output15d(dF3), .output16d(dG3));  // open: coreout0, clockout0, freqout0, output1r, output2r, output4r, output5r, output6r, output7r, output8r, output9r, output10r, output11r, output12r, output13r, output14r, output15r, output16r
  core core7 (
    .corein0(64'hf600e6000f0006), .clockin0(c0), .freqin0(64'h5000000000), .input0(input7), .input1r(r1),
    .input2r(r2), .input3r(r3), .input4r(r4), .input5r(r5), .input6r(r6), .input7r(r7), .input8r(r8),
    .input9r(r9), .input10r(r10), .input11r(r11), .input12r(r12), .input13r(r13), .input14r(r14),
    .input1r5(r15), .input16r(r16), .input1d(d71), .input2d(d72), .input3d(d73), .input4d(d74),
    .input5d(d75), .input6d(d76), .input7d(d77), .input8d(d78), .input9d(d79), .input10d(d7A),
    .input11d(d7B), .input12d(d7C), .input13d(d7D), .input14d(d7E), .input15d(d7F), .input16d(d7G),
    .output0(output7), .output7r(r7), .output1d(d17), .output2d(d27), .output3d(d37), .output4d(d47),
    .output5d(d57), .output6d(d67), .output7d(d77), .output8d(d87), .output9d(d97), .output10d(dA7),
    .output11d(dB7), .output12d(dC7), .output13d(dD7), .output14d(dE7), .output15d(dF7), .output16d(dG7));  // open: coreout0, clockout0, freqout0, output1r, output2r, output3r, output4r, output5r, output6r, output8r, output9r, output10r, output11r, output12r, output13r, output14r, output15r, output16r
  core coreB (
    .corein0(64'hfa00ea000f000a), .clockin0(c0), .freqin0(64'h5000000000), .input0(input11), .input1r(r1),
    .input2r(r2), .input3r(r3), .input4r(r4), .input5r(r5), .input6r(r6), .input7r(r7), .input8r(r8),
    .input9r(r9), .input10r(r10), .input11r(r11), .input12r(r12), .input13r(r13), .input14r(r14),
    .input1r5(r15), .input16r(r16), .input1d(dB1), .input2d(dB2), .input3d(dB3), .input4d(dB4),
    .input5d(dB5), .input6d(dB6), .input7d(dB7), .input8d(dB8), .input9d(dB9), .input10d(dBA),
    .input11d(dBB), .input12d(dBC), .input13d(dBD), .input14d(dBE), .input15d(dBF), .input16d(dBG),
    .output0(output11), .output11r(r11), .output1d(d1B), .output2d(d2B), .output3d(d3B), .output4d(d4B),
    .output5d(d5B), .output6d(d6B), .output7d(d7B), .output8d(d8B), .output9d(d9B), .output10d(dAB),
    .output11d(dBB), .output12d(dCB), .output13d(dDB), .output14d(dEB), .output15d(dFB), .output16d(dGB));  // open: coreout0, clockout0, freqout0, output1r, output2r, output3r, output4r, output5r, output6r, output7r, output8r, output9r, output10r, output12r, output13r, output14r, output15r, output16r
  core coreF (
    .corein0(64'hfe00ee000f000e), .clockin0(c0), .freqin0(64'h5000000000), .input0(input15), .input1r(r1),
    .input2r(r2), .input3r(r3), .input4r(r4), .input5r(r5), .input6r(r6), .input7r(r7), .input8r(r8),
    .input9r(r9), .input10r(r10), .input11r(r11), .input12r(r12), .input13r(r13), .input14r(r14),
    .input1r5(r15), .input16r(r16), .input1d(dF1), .input2d(dF2), .input3d(dF3), .input4d(dF4),
    .input5d(dF5), .input6d(dF6), .input7d(dF7), .input8d(dF8), .input9d(dF9), .input10d(dFA),
    .input11d(dFB), .input12d(dFC), .input13d(dFD), .input14d(dFE), .input15d(dFF), .input16d(dFG),
    .output0(output15), .output15r(r15), .output1d(d1F), .output2d(d2F), .output3d(d3F), .output4d(d4F),
    .output5d(d5F), .output6d(d6F), .output7d(d7F), .output8d(d8F), .output9d(d9F), .output10d(dAF),
    .output11d(dBF), .output12d(dCF), .output13d(dDF), .output14d(dEF), .output15d(dFF), .output16d(dGF));  // open: coreout0, clockout0, freqout0, output1r, output2r, output3r, output4r, output5r, output6r, output7r, output8r, output9r, output10r, output11r, output12r, output13r, output14r, output16r
  core core4 (
    .corein0(64'hf300e3000f0003), .clockin0(c0), .freqin0(64'h5000000000), .input0(input4), .input1r(r1),
    .input2r(r2), .input3r(r3), .input4r(r4), .input5r(r5), .input6r(r6), .input7r(r7), .input8r(r8),
    .input9r(r9), .input10r(r10), .input11r(r11), .input12r(r12), .input13r(r13), .input14r(r14),
    .input1r5(r15), .input16r(r16), .input1d(d41), .input2d(d42), .input3d(d43), .input4d(d44),
    .input5d(d45), .input6d(d46), .input7d(d47), .input8d(d48), .input9d(d49), .input10d(d4A),
    .input11d(d4B), .input12d(d4C), .input13d(d4D), .input14d(d4E), .input15d(d4F), .input16d(d4G),
    .output0(output4), .output4r(r4), .output1d(d14), .output2d(d24), .output3d(d34), .output4d(d44),
    .output5d(d54), .output6d(d64), .output7d(d74), .output8d(d84), .output9d(d94), .output10d(dA4),
    .output11d(dB4), .output12d(dC4), .output13d(dD4), .output14d(dE4), .output15d(dF4), .output16d(dG4));  // open: coreout0, clockout0, freqout0, output1r, output2r, output3r, output5r, output6r, output7r, output8r, output9r, output10r, output11r, output12r, output13r, output14r, output15r, output16r
  core core8 (
    .corein0(64'hf700e7000f0007), .clockin0(c0), .freqin0(64'h5000000000), .input0(input8), .input1r(r1),
    .input2r(r2), .input3r(r3), .input4r(r4), .input5r(r5), .input6r(r6), .input7r(r7), .input8r(r8),
    .input9r(r9), .input10r(r10), .input11r(r11), .input12r(r12), .input13r(r13), .input14r(r14),
    .input1r5(r15), .input16r(r16), .input1d(d81), .input2d(d82), .input3d(d83), .input4d(d84),
    .input5d(d85), .input6d(d86), .input7d(d87), .input8d(d88), .input9d(d89), .input10d(d8A),
    .input11d(d8B), .input12d(d8C), .input13d(d8D), .input14d(d8E), .input15d(d8F), .input16d(d8G),
    .output0(output8), .output8r(r8), .output1d(d18), .output2d(d28), .output3d(d38), .output4d(d48),
    .output5d(d58), .output6d(d68), .output7d(d78), .output8d(d88), .output9d(d98), .output10d(dA8),
    .output11d(dB8), .output12d(dC8), .output13d(dD8), .output14d(dE8), .output15d(dF8), .output16d(dG8));  // open: coreout0, clockout0, freqout0, output1r, output2r, output3r, output4r, output5r, output6r, output7r, output9r, output10r, output11r, output12r, output13r, output14r, output15r, output16r
  core coreC (
    .corein0(64'hfb00eb000f000b), .clockin0(c0), .freqin0(64'h5000000000), .input0(input12), .input1r(r1),
    .input2r(r2), .input3r(r3), .input4r(r4), .input5r(r5), .input6r(r6), .input7r(r7), .input8r(r8),
    .input9r(r9), .input10r(r10), .input11r(r11), .input12r(r12), .input13r(r13), .input14r(r14),
    .input1r5(r15), .input16r(r16), .input1d(dC1), .input2d(dC2), .input3d(dC3), .input4d(dC4),
    .input5d(dC5), .input6d(dC6), .input7d(dC7), .input8d(dC8), .input9d(dC9), .input10d(dCA),
    .input11d(dCB), .input12d(dCC), .input13d(dCD), .input14d(dCE), .input15d(dCF), .input16d(dCG),
    .output0(output12), .output12r(r12), .output1d(d1C), .output2d(d2C), .output3d(d3C), .output4d(d4C),
    .output5d(d5C), .output6d(d6C), .output7d(d7C), .output8d(d8C), .output9d(d9C), .output10d(dAC),
    .output11d(dBC), .output12d(dCC), .output13d(dDC), .output14d(dEC), .output15d(dFC), .output16d(dGC));  // open: coreout0, clockout0, freqout0, output1r, output2r, output3r, output4r, output5r, output6r, output7r, output8r, output9r, output10r, output11r, output13r, output14r, output15r, output16r
  core coreG (
    .corein0(64'hff00ef000f000f), .clockin0(c0), .freqin0(64'h5000000000), .input0(input16), .input1r(r1),
    .input2r(r2), .input3r(r3), .input4r(r4), .input5r(r5), .input6r(r6), .input7r(r7), .input8r(r8),
    .input9r(r9), .input10r(r10), .input11r(r11), .input12r(r12), .input13r(r13), .input14r(r14),
    .input1r5(r15), .input16r(r16), .input1d(dG1), .input2d(dG2), .input3d(dG3), .input4d(dG4),
    .input5d(dG5), .input6d(dG6), .input7d(dG7), .input8d(dG8), .input9d(dG9), .input10d(dGA),
    .input11d(dGB), .input12d(dGC), .input13d(dGD), .input14d(dGE), .input15d(dGF), .input16d(dGG),
    .output0(output16), .output16r(r16), .output1d(d1G), .output2d(d2G), .output3d(d3G), .output4d(d4G),
    .output5d(d5G), .output6d(d6G), .output7d(d7G), .output8d(d8G), .output9d(d9G), .output10d(dAG),
    .output11d(dBG), .output12d(dCG), .output13d(dDG), .output14d(dEG), .output15d(dFG), .output16d(dGG));  // open: coreout0, clockout0, freqout0, output1r, output2r, output3r, output4r, output5r, output6r, output7r, output8r, output9r, output10r, output11r, output12r, output13r, output14r, output15r
  Counter #(.max('hffffffffffffffff), .width(64)) counter_1 (
    .Q(c0), .clk(clock_1_out));  // open: load, D, count, carry, up, clr
  Clock clock_1 (.out(clock_1_out));
endmodule
